# Fritzing sketch teclado_capacitivo (saved by Fritzing 0.9.3b)
breadboards: 1

parts:
  Pro_Micro1 = SparkFun Pro Micro  # not connected
  Pro_Micro3 = Pro Micro  # not connected
  R1 = Resistor [tolerance=±5% resistance=100k package="0603 [SMD]"]
  R2 = Resistor [tolerance=±5% resistance=220 package=THT]
  LED1 = smd LED [color="Red (633nm)" package="0805 [SMD]"]
  C1 = Film/Foil Capacitor [capacitance=100nF voltage=35V package="27.5mm [THT, pp]"]

nets:
  N1: R1.Pin_0, C1.+
  N2: R2.Pin_1, LED1.anode

notes:
  100k ou mais
  220 ohms
  Fio conectado a qualquer material condutivo
  Arduino Micro ou Pro Micro

custom parts:
  SparkFun Pro Micro: The Pro Micro is similar to the Pro Mini except with an ATmega32U4 on board. The USB transceiver inside the 32U4 allows us to add USB connectivity on-board and do away with bulky external USB interface. Based on: https://github.com/unorthodox-engineers/unorthodox-arduino/blob/master/Unorthodox/fritzing/parts/Pro%20Micro.fzpz
  Pro Micro: The SparkFun Pro Micro is a complete USB-based microcontoller development system, in a very small footprint, capable of implementing many types of projects. All programming can be done via the USB port.
